# Fritzing sketch original_layout (saved by Fritzing 0.9.3b)
breadboards: 1

parts:
  Part1 = Adafruit Feather HUZZAH ESP8266 [part_number="Adafruit #2821"]
  CAL = Toggle Switch [package=THT]
  U4 = POT [package=3362u]
  Part2 = Soil Moisture Sensor
  R2 = Resistor [tolerance=±5% resistance=10k package=THT]
  R3 = Resistor [tolerance=±5% resistance=1k package=THT]
  LED2 = smd LED [color="Red (633nm)" package="0805 [SMD]"]
  D1 = Diode [package=diode-1n4001]
  NEOPIXEL1 = Neopixel Strip -- Black (30/m) [part_number=1376]
  C2 = Capacitor Polarized [package=cpol-radial-100uf-25v]
  CAL1 = Toggle Switch [package=THT]

nets:
  N1: Part1.GPIO14/SCK, R3.Pin_0
  N2: Part1.ADC, U4.S, R2.Pin_0
  GND: Part1.GND, CAL.L2, Part2.GND, R2.Pin_1, LED2.cathode, NEOPIXEL1.GND, C2.-, CAL1.L1
  N3: Part1.3.3V, CAL.L1
  N4: Part1.VBUS, C2.+, CAL1.L2
  N5: Part1.GPIO0, NEOPIXEL1.Din
  N6: Part1.GPIO2, CAL.COM
  N7: U4.E, Part2.SIG
  N8: Part2.VCC, D1.C
  N9: R3.Pin_1, LED2.anode
  N10: NEOPIXEL1.+5V, CAL1.COM

custom parts:
  Adafruit Feather HUZZAH ESP8266: his is the Adafruit Feather HUZZAH ESP8266 - our take on an 'all-in-one' ESP8266 WiFi development board with built in USB and battery charging. Its an ESP8266 WiFi module with all the extras you need, ready to rock! We have other boards in the Feather family, check'em out here. At the Feather HUZZAH's heart is an ESP8266 WiFi microcontroller clocked at 80 MHz and at 3.3V logic. This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
  Neopixel Strip -- Black (30/m): These NeoPixel strips have 30 digitally-addressable pixel LEDs per meter and are very affordable and are only 12.5 mm wide, 10 mm if you remove the strip from the casing.
