# Fritzing sketch strip_board_layout (saved by Fritzing 0.9.3b)
stripboards: 1

parts:
  Part3 = Adafruit Feather HUZZAH ESP8266 [part_number="Adafruit #2821"]
  U5 = POT [package=3362u]
  R4 = Resistor [tolerance=±5% resistance=10k package=THT]
  D2 = Diode [package=diode-1n4001]
  R5 = Resistor [tolerance=±5% resistance=1k package=THT]
  LED3 = smd LED [color="Red (633nm)" package="0805 [SMD]"]
  CAL2 = Toggle Switch [package=THT]
  C3 = Capacitor Polarized [package=cpol-radial-100uf-25v]
  CAL3 = Toggle Switch [package=THT]

nets:
  N1: Part3.GPIO14/SCK, D2.A, R5.Pin_0
  N2: Part3.ADC, U5.S
  N3: Part3.GND, R4.Pin_1, LED3.cathode, CAL2.L1, C3.-, CAL3.L1
  N4: Part3.3.3V, CAL2.L2
  N5: Part3.VBUS, C3.+, CAL3.L2
  N6: Part3.GPIO2, CAL2.COM
  N7: U5.E, R4.Pin_0
  N8: R5.Pin_1, LED3.anode

custom parts:
  Adafruit Feather HUZZAH ESP8266: his is the Adafruit Feather HUZZAH ESP8266 - our take on an 'all-in-one' ESP8266 WiFi development board with built in USB and battery charging. Its an ESP8266 WiFi module with all the extras you need, ready to rock! We have other boards in the Feather family, check'em out here. At the Feather HUZZAH's heart is an ESP8266 WiFi microcontroller clocked at 80 MHz and at 3.3V logic. This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
